// Logisim project q8.circ as structural Verilog: 4 circuits, main circuit main
module main (
  input  A,
  input  B,
  input  C,
  output X
);

  wire and_1_out;

  and and_1 (and_1_out, A, B);
  or or_1 (X, and_1_out, C);
endmodule

module b (
  input  A,
  input  B,
  input  C,
  output X
);

  wire not_1_out, or_1_out;

  not not_1 (not_1_out, A);
  or or_1 (or_1_out, B, C);
  and and_1 (X, not_1_out, or_1_out);
endmodule

module c (
  input  A,
  input  B,
  input  C,
  output X
);

  wire and_1_out, nand_1_out;

  and and_1 (and_1_out, B, C);
  nand nand_1 (nand_1_out, A, B);
  or or_1 (X, nand_1_out, and_1_out);
endmodule

module d (
  input  A,
  input  B,
  input  C,
  output X
);

  wire not_1_out, xor_1_out;

  xor xor_1 (xor_1_out, A, B);
  and and_1 (X, xor_1_out, not_1_out);
  not not_1 (not_1_out, C);
endmodule
